# Fritzing sketch veliero_1.1 (saved by Fritzing 0.8.3b)
circuit board: 6.88561cm x 5.36311cm
breadboards: 1

parts:
  J2 = female pin header, 6 pins [form="♀ (female)"]
  J1 = female pin header, 8 pins [form="♀ (female)"]
  J3 = female pin header, 8 pins [form="♀ (female)"]
  J4 = female pin header, 6 pins [form="♀ (female)"]
  U1 = atmega328 [package=dip]
  VIN = Power Jack [package=power_jack_pth]
  C2 = Electrolytic Capacitor [capacitance=10µF voltage=16V package="100 mil [THT, electrolytic]"]
  R1 = Resistor [tolerance=±5% resistance=10k package=THT]
  XTAL1 = Crystal [frequency="16 Mhz" package=THT]
  C1 = Ceramic Capacitor [capacitance="100 nF" package="200 mil [THT, multilayer]"]
  C5 = Ceramic Capacitor [capacitance="100 nF" package="200 mil [THT, multilayer]"]
  J5 = AVR ISP 6 Pin [package=2x3]
  R2 = Resistor [tolerance=±5% resistance=1k package=THT]
  C6 = Ceramic Capacitor [capacitance="100 nF" package="200 mil [THT, multilayer]"]
  LED1 = LED - 3mm [color="Red (633nm)" package="3 mm [THT]"]
  C3 = Ceramic Capacitor [capacitance=22µF package="100 mil [THT, multilayer]"]
  C4 = Ceramic Capacitor [capacitance=22µF package="100 mil [THT, multilayer]"]
  S1 = Pushbutton [package=THT]
  JP1 = female pin header, 2 pins [form="♀ (female)"]
  IC1 = Voltage Regulator [package=to-92]
  C7 = Ceramic Capacitor [capacitance="100 nF" package="200 mil [THT, multilayer]"]

nets:
  N1: J2.pin1, U1.A5
  N2: J2.pin2, U1.A4
  N3: J2.pin3, U1.A3
  N4: J2.pin4, U1.A2
  N5: J2.pin5, U1.A1
  N6: J2.pin6, U1.A0
  N7: J1.pin1, U1.D0_(RX)
  N8: J1.pin2, U1.D1_(TX)
  N9: J1.pin3, U1.D2
  N10: J1.pin4, U1.D3_(PWM)
  N11: J1.pin5, U1.D4
  N12: J1.pin6, U1.D5_(PWM)
  N13: J1.pin7, U1.D6_(PWM)
  N14: J1.pin8, U1.D7
  N15: J3.pin1, U1.D8
  N16: J3.pin2, U1.D9_(PWM)
  N17: J3.pin3, U1.D10_(PWM)
  N18: J3.pin4, U1.D11_(PWM), J5.4
  N19: J3.pin5, U1.D12, J5.1
  N20: J3.pin6, U1.D13, J5.3, R2.Pin_1
  GND: J3.pin7, J4.pin2, J4.pin3, U1.GND, VIN.GND, VIN.GNDBREAK, C2.-, C1.1, C5.1, J5.6, C6.1, LED1.cathode, C3.1, C4.0, S1.leg1, IC1.GND, C7.1
  N21: J3.pin8, U1.AREF, C6.0
  N22: J4.pin1, VIN.PWR, C1.0, JP1.pin2, IC1.IN
  N23: J4.pin4, U1.VCC, U1.AVCC, C2.+, R1.Pin_1, C5.0, J5.2, JP1.pin1, IC1.OUT
  N24: J4.pin6, U1.RESET, R1.Pin_0, J5.5, S1.leg0, C7.0
  N25: U1.XLAT1, XTAL1.pin_1, C4.1
  N26: U1.XLAT2, XTAL1.pin_0, C3.0
  N27: R2.Pin_0, LED1.anode

notes:
  vin
  gnd
  5v
  nc
  rst
  veliero
  microcontroller
  a5
  a4
  a3
  a2
  a1
  a0
  <0
  >1
  2
  •3
  4
  •5
  •6
  7
  8
  •9
  •10
  •11
  12
  13
  aref
  sites.google.com/site/creationsbypeter
  reset
  ARDUINO IDE compatible
  by peter
  Questa cosa prende il suo
  nome dalla parola italiana
  per nave a vela. Le tracce
  Questa cosa prende il suo nome dalla parola italiana per nave a vela. Le tracce hanno l'aspetto di vele.
  hanno l'aspetto di vele.

custom parts:
  Voltage Regulator: Voltage Regulator Standard 7805 5V regulator. IGO (Input Ground Output). Spark Fun Electronics SKU : COM-00107
